// Logisim project hamo.circ as structural Verilog: 1 circuit, main circuit main
module main (
  input  A,
  input  B,
  input  A_2,
  input  B_2,
  input  A_3
);

  wire and_1_out, not_1_out, or_1_out;

  or or_1 (or_1_out, A, B);
  LED led_1 (.in(or_1_out));
  LED led_2 (.in(and_1_out));
  and and_1 (and_1_out, A_2, B_2);
  not not_1 (not_1_out, A_3);
  LED led_3 (.in(not_1_out));

  // Notes on the sheet:
  //   A+B
  //   A.B
  //   Not A
endmodule
